# Fritzing sketch Carro (saved by Fritzing 0.9.3b)
breadboards: 1

parts:
  Componente1 = Arduino Uno (Rev3)
  VCC3 = Battery block 9V  # not connected
  VCC4 = 4 x AAA Battery Mount
  R1 = Resistor [tolerance=±5% resistance=1k package=THT]
  R2 = Resistor [tolerance=±5% resistance=270 package=THT]
  U1 = L9110 H-bridge module [part_number="L9110 H-bridge"]
  MOTOR_DC_6V_direito2 = MOTOR_DC6V
  Motor_DC_Esquerdo2 = Motor DC 6V Esquerdo
  hc-sr1 = hc-sr04
  Power_plug1 = Power plug  # not connected
  Componente2 = Bluetooth HC-05 Macho

nets:
  N1: Componente1.D8, hc-sr1.Echo
  N2: Componente1.D9_PWM, U1.B-IB
  N3: Componente1.D12/MISO, Componente2.TXD
  N4: Componente1.D13/SCK, R2.Pin_1
  N5: Componente1.D3_PWM, U1.A-IA
  N6: Componente1.D5_PWM, U1.A-IB
  N7: Componente1.D6_PWM, U1.B-IA
  N8: Componente1.D7, hc-sr1.Trig
  VCC: Componente1.5V, hc-sr1.VCC, Componente2.VCC
  GND: Componente1.GND, VCC4.-, R1.Pin_1, U1.GND, hc-sr1.GND, Componente2.GND
  N9: VCC4.+, U1.VCC
  N10: R1.Pin_0, R2.Pin_0, Componente2.RXD
  N11: U1.MOTOR_A-A, MOTOR_DC_6V_direito2.VCC
  N12: U1.MOTOR_A-B, MOTOR_DC_6V_direito2.GND
  N13: U1.MOTOR_B-A, Motor_DC_Esquerdo2.GND
  N14: U1.MOTOR_B-B, Motor_DC_Esquerdo2.VCC

custom parts:
  MOTOR_DC6V: Motor dc 6V direito
  Motor DC 6V Esquerdo: Motor dc esquerdo
  Power plug: power plug
